// Logisim project bak.circ as structural Verilog: 3 circuits, main circuit main
module main (
  input  in_1,
  input  in_2,
  input  in_3,
  input  DEBUG,
  input  in_5,
  input  in_6,
  input  in_7,
  input  in_8,
  input  in_9,
  input  in_10,
  input  in_11,
  input  in_12,
  input  in_13,
  input  in_14,
  input  in_15,
  input  in_16,
  input  in_17,
  input  in_18,
  input  in_19,
  input  in_20,
  input  in_21,
  input  in_22,
  input  in_23,
  input  in_24,
  input  in_25,
  input  in_26,
  input  in_27,
  input  in_28,
  input  in_29
);

  wire ADD_C, ADR_IN, ALU_CARRY, ALU_EQ, ALU_G, ALU_L, ALU_ZERO, and_2_out, button_2_out, CLK,
       comparator_1_eq, comparator_1_gt, comparator_1_lt, comparator_2_eq, CONSTANTV_0, CONSTANTV_1,
       d_ff_1_qn, FLAG_COND_0, FLAG_COND_1, FLAG_COND_2, FLAG_FALSE, HALT, HALTED, INS_IN, JMP_IN,
       MICROCODE_END, not_1_out, not_2_out, not_3_out, not_4_out, not_5_out, not_6_out, or_1_out, PC_COUNT,
       R1IN, R2IN, R3IN, R4IN, R5IN, R6IN, R7IN, R8IN, RAM_IN, REG_IN_0, REG_IN_1, REG_IN_2, REG_IN_3,
       REG_OUT_0, REG_OUT_1, REG_OUT_2, REG_OUT_3, RESET, SP_COUNT, SP_DEC, SP_IN, SUB_C, UPDATE_FLAGS,
       USE_INS_A_IN, USE_INS_A_OUT, USE_INS_B_IN, USE_INS_B_OUT;
  wire [3:0] ALU_OP, bitselector_1_out, counter_2_q, multiplexer_4_out, multiplexer_5_out, multiplexer_6_out,
       multiplexer_7_out;
  wire [4:0] bitselector_3_out, bitselector_4_out, bitselector_5_out, bitselector_6_out, bitselector_7_out,
       register_1_q;
  wire [7:0] INS_OPCODE;
  wire [15:0] bitselector_2_out;
  wire [23:0] INS_OUT;
  wire [27:0] MICROCODE;
  wire [27:27] multiplexer_1_out;
  wire [31:0] adder_1_out, ADR_OUT, ALU_A, ALU_B, ALU_OUT, bitwisealu_p3, bitwisealu_p4, bitwisealu_p5,
       bitwisealu_p6, bitwisealu_p7, CONSTANT_OUT, DBUS, INS_LITERAL, multiplier_1_out, negator_1_out,
       PC_OUT, R1OUT, R2OUT, R3OUT, R4OUT, R5OUT, R6OUT, R7OUT, R8OUT, RAM_OUT, shifter_1_out, shifter_2_out,
       shifter_3_out, shifter_4_out, shifter_5_out, SP_OUT, subtractor_1_out;

  LedBar ledbar_1 (
    .led0(INS_OPCODE[7]), .led1(INS_OPCODE[6]), .led2(INS_OPCODE[5]), .led3(INS_OPCODE[4]),
    .led4(INS_OPCODE[3]), .led5(INS_OPCODE[2]), .led6(INS_OPCODE[1]), .led7(INS_OPCODE[0]));
  Register #(.width(32)) R1 (.D(DBUS), .en(R1IN), .clk(CLK), .Q(R1OUT), .clr(RESET));
  Register #(.width(32)) R2 (.D(DBUS), .en(R2IN), .clk(CLK), .Q(R2OUT), .clr(RESET));
  Register #(.width(32)) R3 (.D(DBUS), .en(R3IN), .clk(CLK), .Q(R3OUT), .clr(RESET));
  Register #(.width(32)) R4 (.D(DBUS), .en(R4IN), .clk(CLK), .Q(R4OUT), .clr(RESET));
  Register #(.width(32)) R5 (.D(DBUS), .en(R5IN), .clk(CLK), .Q(R5OUT), .clr(RESET));
  Register #(.width(32)) R6 (.D(DBUS), .en(R6IN), .clk(CLK), .Q(R6OUT), .clr(RESET));
  Register #(.width(32)) R7 (.D(DBUS), .en(R7IN), .clk(CLK), .Q(R7OUT), .clr(RESET));
  Register #(.width(32)) R8 (.D(DBUS), .en(R8IN), .clk(CLK), .Q(R8OUT), .clr(RESET));
  Register #(.width(32)) RINS (.D(DBUS), .en(INS_IN), .clk(CLK), .Q({INS_OPCODE, INS_OUT}), .clr(RESET));
  LedBar #(.matrixcols(4)) ledbar_2 (.led0(INS_OUT[23]), .led1(INS_OUT[22]), .led2(INS_OUT[21]), .led3(INS_OUT[20]));
  LedBar #(.matrixcols(4)) ledbar_3 (.led0(INS_OUT[19]), .led1(INS_OUT[18]), .led2(INS_OUT[17]), .led3(INS_OUT[16]));
  not not_1 (not_1_out, SP_DEC);
  Counter #(.max('hffffffff), .width(32)) counter_1 (
    .load(SP_IN), .D(DBUS), .count(SP_COUNT), .Q(SP_OUT), .up(not_1_out), .clk(CLK), .clr(RESET));  // open: carry
  LedBar #(.matrixcols(16)) ledbar_4 (
    .led0(INS_OUT[15]), .led1(INS_OUT[14]), .led2(INS_OUT[13]), .led3(INS_OUT[12]), .led4(INS_OUT[11]),
    .led5(INS_OUT[10]), .led6(INS_OUT[9]), .led7(INS_OUT[8]), .led8(INS_OUT[7]), .led9(INS_OUT[6]),
    .led10(INS_OUT[5]), .led11(INS_OUT[4]), .led12(INS_OUT[3]), .led13(INS_OUT[2]), .led14(INS_OUT[1]),
    .led15(INS_OUT[0]));
  assign INS_LITERAL = {{16{1'b0}}, INS_OUT[15:0]};  // Bit_Extender bit_extender_1
  LedBar #(.matrixcols(4)) OUT_LEDS (
    .led0(bitselector_1_out[3]), .led1(bitselector_1_out[2]), .led2(bitselector_1_out[1]),
    .led3(bitselector_1_out[0]));
  D_Flip_Flop d_ff_1 (.D(1'b0), .clk(1'b0), .Q(HALTED), .Qn(d_ff_1_qn), .preset(HALT), .reset(RESET));
  BitSelector #(.group(4), .width(32)) bitselector_1 (.in(DBUS), .out(bitselector_1_out), .sel(3'b000));
  Counter #(.max('hf), .width(4)) counter_2 (
    .load(1'b0), .count(1'b1), .Q(counter_2_q), .up(1'b1), .clk(CLK), .clr(or_1_out));  // open: D, carry
  or or_1 (or_1_out, RESET, FLAG_FALSE, MICROCODE_END);
  Register #(.width(32)) RADR (.D(DBUS), .en(ADR_IN), .clk(CLK), .Q(ADR_OUT), .clr(RESET));
  // Probe on DBUS
  RAM #(.addrWidth(16), .asyncread("true"), .dataWidth(32), .\type ("nonvolatile")) ram_1 (
    .addr(bitselector_2_out), .we(RAM_IN), .oe(1'b1), .clk(CLK), .din(DBUS), .dout(RAM_OUT));
  BitSelector #(.group(16), .width(32)) bitselector_2 (.in(ADR_OUT), .out(bitselector_2_out), .sel(1'b0));
  and and_1 (CLK, button_2_out, d_ff_1_qn);
  Multiplexer #(.width(28)) multiplexer_1 (
    .in0(MICROCODE),
    .in1({in_29, in_28, in_27, in_26, in_25, in_24, in_23, in_22, in_21, in_20, in_19, in_18, in_17, in_16, in_15, in_14, in_13, in_12, in_11, in_10, in_9, in_8, in_7, in_6, in_5, in_3, in_2, in_1}),
    .out({multiplexer_1_out[27], FLAG_COND_2, FLAG_COND_1, FLAG_COND_0, HALT, UPDATE_FLAGS, SP_DEC, USE_INS_B_IN, USE_INS_A_IN, USE_INS_B_OUT, USE_INS_A_OUT, SP_COUNT, MICROCODE_END, PC_COUNT, ALU_OP, CONSTANTV_0, CONSTANTV_1, REG_OUT_3, REG_OUT_2, REG_OUT_1, REG_OUT_0, REG_IN_3, REG_IN_2, REG_IN_1, REG_IN_0}));  // open: sel
  ROM #(.addrWidth(12), .dataWidth(28)) rom_1 (.addr({INS_OPCODE, counter_2_q}), .data(MICROCODE));
  Button button_1 (.out(RESET));
  Button button_2 (.out(button_2_out));
  Multiplexer #(.select(2), .width(32)) multiplexer_2 (
    .in0({32{1'b0}}), .in1(32'h1), .in2({32{1'b1}}), .out(CONSTANT_OUT), .sel({CONSTANTV_0, CONSTANTV_1}));  // open: in3
  Demultiplexer #(.select(4)) demultiplexer_1 (
    .out1(R1IN), .out2(R2IN), .out3(R3IN), .out4(R4IN), .out5(R5IN), .out6(R6IN), .out7(R7IN), .out8(R8IN),
    .out9(RAM_IN), .out10(INS_IN), .out11(ADR_IN), .out12(JMP_IN), .out15(SP_IN), .in(1'b1),
    .sel(multiplexer_4_out));  // open: out0, out13, out14
  Multiplexer #(.select(4), .width(32)) multiplexer_3 (
    .in0({32{1'b0}}), .in1(R1OUT), .in2(R2OUT), .in3(R3OUT), .in4(R4OUT), .in5(R5OUT), .in6(R6OUT),
    .in7(R7OUT), .in8(R8OUT), .in9(RAM_OUT), .in10(INS_LITERAL), .in11(ADR_OUT), .in12(PC_OUT),
    .in13(CONSTANT_OUT), .in14(ALU_OUT), .in15(SP_OUT), .out(DBUS), .sel(multiplexer_7_out));
  Counter #(.max('hffffffff), .width(32)) counter_3 (
    .load(JMP_IN), .D(DBUS), .count(PC_COUNT), .Q(PC_OUT), .up(1'b1), .clk(CLK), .clr(RESET));  // open: carry
  Multiplexer #(.width(4)) multiplexer_4 (
    .in0(multiplexer_5_out), .in1(INS_OUT[19:16]), .out(multiplexer_4_out), .sel(USE_INS_B_IN));
  Multiplexer #(.width(4)) multiplexer_5 (
    .in0({REG_IN_3, REG_IN_2, REG_IN_1, REG_IN_0}), .in1(INS_OUT[23:20]), .out(multiplexer_5_out),
    .sel(USE_INS_A_IN));
  Multiplexer #(.width(4)) multiplexer_6 (
    .in0({REG_OUT_3, REG_OUT_2, REG_OUT_1, REG_OUT_0}), .in1(INS_OUT[23:20]), .out(multiplexer_6_out),
    .sel(USE_INS_A_OUT));
  Register #(.width(5)) register_1 (
    .D({ALU_CARRY, ALU_G, ALU_EQ, ALU_L, ALU_ZERO}), .en(UPDATE_FLAGS), .clk(CLK), .Q(register_1_q),
    .clr(RESET));
  Multiplexer #(.width(4)) multiplexer_7 (
    .in0(multiplexer_6_out), .in1(INS_OUT[19:16]), .out(multiplexer_7_out), .sel(USE_INS_B_OUT));
  LED led_1 (.in(register_1_q[0]));
  LED led_2 (.in(register_1_q[1]));
  LED led_3 (.in(register_1_q[2]));
  LED led_4 (.in(register_1_q[3]));
  LED led_5 (.in(register_1_q[4]));
  BitSelector #(.group(5), .width(32)) bitselector_3 (.in(ALU_B), .out(bitselector_3_out), .sel(3'b000));
  BitSelector #(.group(5), .width(32)) bitselector_4 (.in(ALU_B), .out(bitselector_4_out), .sel(3'b000));
  BitSelector #(.group(5), .width(32)) bitselector_5 (.in(ALU_B), .out(bitselector_5_out), .sel(3'b000));
  BitSelector #(.group(5), .width(32)) bitselector_6 (.in(ALU_B), .out(bitselector_6_out), .sel(3'b000));
  BitSelector #(.group(5), .width(32)) bitselector_7 (.in(ALU_B), .out(bitselector_7_out), .sel(3'b000));
  not not_2 (not_2_out, register_1_q[0]);
  not not_3 (not_3_out, register_1_q[1]);
  not not_4 (not_4_out, register_1_q[3]);
  not not_5 (not_5_out, register_1_q[2]);
  not not_6 (not_6_out, register_1_q[4]);
  Adder #(.width(32)) adder_1 (.a(ALU_A), .b(ALU_B), .out(adder_1_out), .cin(1'b0), .cout(ADD_C));
  Subtractor #(.width(32)) subtractor_1 (.a(ALU_A), .b(ALU_B), .out(subtractor_1_out), .bin(1'b0), .bout(SUB_C));
  Multiplier #(.width(32)) multiplier_1 (.a(ALU_A), .b(ALU_B), .out(multiplier_1_out));  // open: cin, cout
  Negator #(.width(32)) negator_1 (.in(ALU_A), .out(negator_1_out));
  Shifter #(.width(32)) shifter_1 (.in(ALU_A), .\dist (bitselector_3_out), .out(shifter_1_out));
  Shifter #(.shift("lr"), .width(32)) shifter_2 (.in(ALU_A), .\dist (bitselector_4_out), .out(shifter_2_out));
  Shifter #(.shift("ar"), .width(32)) shifter_3 (.in(ALU_A), .\dist (bitselector_5_out), .out(shifter_3_out));
  Shifter #(.shift("rl"), .width(32)) shifter_4 (.in(ALU_A), .\dist (bitselector_6_out), .out(shifter_4_out));
  Shifter #(.shift("rr"), .width(32)) shifter_5 (.in(ALU_A), .\dist (bitselector_7_out), .out(shifter_5_out));
  Comparator #(.width(32)) comparator_1 (
    .a(ALU_A), .b(ALU_B), .gt(comparator_1_gt), .eq(comparator_1_eq), .lt(comparator_1_lt));
  // bitwiseOps bitwisealu: pin names not known; wires that end beside it: ALU_A, ALU_B, bitwisealu_p3, bitwisealu_p4, bitwisealu_p5, bitwisealu_p6, bitwisealu_p7
  Multiplexer #(.select(4), .width(32)) multiplexer_8 (
    .in0({32{1'b0}}), .in1(R1OUT), .in2(R2OUT), .in3(R3OUT), .in4(R4OUT), .in5(R5OUT), .in6(R6OUT),
    .in7(R7OUT), .in8(R8OUT), .in9(RAM_OUT), .in10(INS_LITERAL), .in11(ADR_OUT), .in12(PC_OUT),
    .in13(CONSTANT_OUT), .in14(ALU_OUT), .in15(SP_OUT), .out(ALU_A), .sel(INS_OUT[23:20]));
  Multiplexer #(.select(3)) multiplexer_9 (
    .in0(1'b0), .in1(register_1_q[0]), .in2(not_2_out), .in3(not_3_out), .in4(not_4_out), .in5(not_5_out),
    .in6(register_1_q[2]), .in7(not_6_out), .out(FLAG_FALSE), .sel({FLAG_COND_2, FLAG_COND_1, FLAG_COND_0}));
  alucarry alucarry_1 (.ALU_CARRY(ALU_CARRY), .SUB_C(SUB_C), .ALU_OP(ALU_OP), .ADD_C(ADD_C));
  Multiplexer #(.select(4), .width(32)) multiplexer_10 (
    .in0({32{1'b0}}), .in1(adder_1_out), .in2(subtractor_1_out), .in3(multiplier_1_out), .in4(negator_1_out),
    .in5(shifter_1_out), .in6(shifter_2_out), .in7(shifter_3_out), .in8(shifter_4_out), .in9(shifter_5_out),
    .in10({32{1'b0}}), .in11(bitwisealu_p3), .in12(bitwisealu_p4), .in13(bitwisealu_p5),
    .in14(bitwisealu_p6), .in15(bitwisealu_p7), .out(ALU_OUT), .sel(ALU_OP));
  and and_2 (and_2_out, 1'b1, ALU_OP[3], ~ALU_OP[2], ALU_OP[1], ~ALU_OP[0]);  // AND_Gate
  and and_3 (ALU_G, and_2_out, comparator_1_gt);
  and and_4 (ALU_L, and_2_out, comparator_1_lt);
  and and_5 (ALU_ZERO, comparator_2_eq, ~and_2_out);  // AND_Gate
  and and_6 (ALU_EQ, and_2_out, comparator_1_eq);
  Comparator #(.width(32)) comparator_2 (.a(ALU_OUT), .b({32{1'b0}}), .eq(comparator_2_eq));  // open: gt, lt
  Multiplexer #(.select(4), .width(32)) multiplexer_11 (
    .in0({32{1'b0}}), .in1(R1OUT), .in2(R2OUT), .in3(R3OUT), .in4(R4OUT), .in5(R5OUT), .in6(R6OUT),
    .in7(R7OUT), .in8(R8OUT), .in9(RAM_OUT), .in10(INS_LITERAL), .in11(ADR_OUT), .in12(PC_OUT),
    .in13(CONSTANT_OUT), .in14(ALU_OUT), .in15(SP_OUT), .out(ALU_B), .sel(INS_OUT[19:16]));

  // Other names for the same wires on the sheet: INS_OUT[31:24] = INS_OPCODE; ALU_OP_0 = ALU_OP[0];
  //   ALU_OP_1 = ALU_OP[1]; ALU_OP_2 = ALU_OP[2]; ALU_OP_3 = ALU_OP[3]; INS_REG_B[3:0] = INS_OUT[19:16];
  //   INS_REG_A[3:0] = INS_OUT[23:20]

  // Notes on the sheet:
  //   REGISTERS
  //   CONTROL
  //   MICROCODE ROM
  //   contents of rom_1 (hex, n*v repeats v):
  //   cb 409a 8000 13*0 cb 409a 8000 13*0 cb 409a 8000 13*0 cb 409a 8000 13*0 cb 409a 8000 13*0 cb 409a
  //   8000 13*0 cb 409a 8000 13*0 cb 409a 8000 13*0 cb 409a 8000 13*0 cb 409a 8000 13*0 cb 409a 8000 13*0
  //   cb 409a 8000 13*0 cb 409a 8000 13*0 cb 409a 8000 13*0 cb 409a 8000 13*0 cb 409a 8000 13*0 cb 409a
  //   8000 13*0 cb 409a 8000 13*0 cb 409a 8000 13*0 cb 409a 4828e0 8000 12*0 cb 409a 804e0 8000 12*0 cb
  //   409a 808e0 8000 12*0 cb 409a 80ce0 8000 12*0 cb 409a 82ce0 8000 12*0 cb 409a 830e0 8000 12*0 cb 409a
  //   834e0 8000 12*0 cb 409a 8000 13*0 cb 409a 8000 13*0 cb 409a 8000 13*0 cb 409a 8000 13*0 cb 409a 8000
  //   13*0 cb 409a 8000 13*0 cb 409a 838e0 8000 12*0 cb 409a 83ce0 8000 12*0 cb 409a 8000 13*0 cb 409a
  //   8000 13*0 cb 409a 8000 13*0 cb 409a 8000 13*0 cb 409a 8000 13*0 cb 409a 8000 13*0 cb 409a 8000 13*0
  //   cb 409a 8000 13*0 cb 409a 8000 13*0 cb 409a 8000 13*0 cb 409a 8000 13*0 cb 409a 8000 13*0 cb 409a
  //   8000 13*0 cb 409a 8000 13*0 cb 409a 8000 13*0 cb 409a 8000 13*0 cb 409a 8000 13*0 cb 409a fb 30009
  //   8000 11*0 cb 409a 210000 fb 80090 8000 10*0 cb 409a 8000 13*0 cb 409a 8000 13*0 cb 409a 8000 13*0 cb
  //   409a 8000 13*0 cb 409a 8000 13*0 cb 409a 8000 13*0 cb 409a 8000 13*0 cb 409a 8000 13*0 cb 409a 8000
  //   13*0 cb 409a 8000 13*0 cb 409a 8000 13*0 cb 409a 8000 13*0 cb 409a 8000 13*0 cb 409a 8000 13*0 cb
  //   409a 8000 13*0 cb 409a 8000 13*0 cb 409a c0000 8000 12*0 cb 409a 800a0 8000 12*0 cb 409a ab 80090
  //   8000 11*0 cb 409a ab 9b 80090 8000 10*0 cb 409a ab 20009 8000 11*0 cb 409a 8000 13*0 cb 409a 8000
  //   13*0 cb 409a 8000 13*0 cb 409a 8000 13*0 cb 409a 8000 13*0 cb 409a 8000 13*0 cb 409a ab 9b 20009
  //   8000 10*0 cb 409a 8000 13*0 cb 409a 8000 13*0 cb 409a 8000 13*0 cb 409a 8000 13*0 cb 409a 8000 13*0
  //   cb 409a 8000 13*0 cb 409a 8000 13*0 cb 409a 8000 13*0 cb 409a 8000 13*0 cb 409a 8000 13*0 cb 409a
  //   8000 13*0 cb 409a 8000 13*0 cb 409a 8000 13*0 cb 409a 8000 13*0 cb 409a 8000 13*0 cb 409a 8000 13*0
  //   cb 409a 8000 13*0 cb 409a 8000 13*0 cb 409a 8000 13*0 cb 409a 8000 13*0 cb 409a 8000 13*0 cb 409a
  //   8000 13*0 cb 409a 8000 13*0 cb 409a 8000 13*0 cb 409a 8000 13*0 cb 409a 8000 13*0 cb 409a 8000 13*0
  //   cb 409a 8000 13*0 cb 409a 8000 13*0 cb 409a 8000 13*0 cb 409a 8000 13*0 cb 409a 8000 13*0 cb 409a
  //   8000 13*0 cb 409a 8000 13*0 cb 409a 8000 13*0 cb 409a 8000 13*0 cb 409a 8000 13*0 cb 409a 8000 13*0
  //   cb 409a 8000 13*0 cb 409a 8000 13*0 cb 409a 8000 13*0 cb 409a 8000 13*0 cb 409a 8000 13*0 cb 409a
  //   8000 13*0 cb 409a 8000 13*0 cb 409a 8000 13*0 cb 409a 8000 13*0 cb 409a 8000 13*0 cb 409a 8000 13*0
  //   cb 409a 8000 13*0 cb 409a 8000 13*0 cb 409a 8000 13*0 cb 409a 8000 13*0 cb 409a 8000 13*0 cb 409a
  //   8000 13*0 cb 409a 8000 13*0 cb 409a 8000 13*0 cb 409a 8000 13*0 cb 409a 8000 13*0 cb 409a 8000 13*0
  //   cb 409a 8000 13*0 cb 409a 8000 13*0 cb 409a 8000 13*0 cb 409a 8000 13*0 cb 409a 8000 13*0 cb 409a
  //   8000 13*0 cb 409a 8000 13*0 cb 409a 8000 13*0 cb 409a 8000 13*0 cb 409a 8000 13*0 cb 409a 8000 13*0
  //   cb 409a 8000 13*0 cb 409a 800000 13*0 cb 409a 8000 13*0 cb 409a 8000 13*0 cb 409a 8000 13*0 cb 409a
  //   8000 13*0 cb 409a 8000 13*0 cb 409a 8000 13*0 cb 409a 8000 13*0 cb 409a 8000 13*0 cb 409a 8000 13*0
  //   cb 409a 8000 13*0 cb 409a 8000 13*0 cb 409a 8000 13*0 cb 409a 8000 13*0 cb 409a 8000 13*0 cb 409a
  //   8000 13*0 cb 409a 8000 13*0 cb 409a 8000 13*0 cb 409a 8000 13*0 cb 409a 8000 13*0 cb 409a 8000 13*0
  //   cb 409a 8000 13*0 cb 409a 8000 13*0 cb 409a 8000 13*0 cb 409a 8000 13*0 cb 409a 8000 13*0 cb 409a
  //   8000 13*0 cb 409a 8000 13*0 cb 409a 8000 13*0 cb 409a 8000 13*0 cb 409a 8000 13*0 cb 409a 8000 13*0
  //   cb 409a 8000 13*0 cb 409a 8000 13*0 cb 409a 8000 13*0 cb 409a 8000 13*0 cb 409a 8000 13*0 cb 409a
  //   8000 13*0 cb 409a 8000 13*0 cb 409a 8000 13*0 cb 409a 8000 13*0 cb 409a 8000 13*0 cb 409a 8000 13*0
  //   cb 409a 8000 13*0 cb 409a 8000 13*0 cb 409a 8000 13*0 cb 409a 8000 13*0 cb 409a 8000 13*0 cb 409a
  //   8000 13*0 cb 409a 8000 13*0 cb 409a 8000 13*0 cb 409a 8000 13*0 cb 409a 8000 13*0 cb 409a 8000 13*0
  //   cb 409a 8000 13*0 cb 409a 8000 13*0 cb 409a 8000 13*0 cb 409a 8000 13*0 cb 409a 8000 13*0 cb 409a
  //   8000 13*0 cb 409a 8000 13*0 cb 409a 8000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
  //   RAM
  //   0
  //   1
  //   -1
  //   unused
  //   LOAD DEMUX
  //   STORE MUX
  //   PROGRAM COUNTER
  //   FLAGS
  //   Z L E G C
  //   ALU
  //   ALU INPUTS MUX
  //   NONE
  //   JNZ
  //   JZ
  //   JL
  //   JG
  //   JE
  //   JNE
  //   JC
endmodule

module alucarry (
  input  ADD_C,
  input  SUB_C,
  input  [3:0] ALU_OP,
  output ALU_CARRY
);

  wire and_1_out, and_2_out, not_1_out, not_2_out, not_3_out, not_4_out;

  not not_1 (not_1_out, ALU_OP[3]);
  not not_2 (not_2_out, ALU_OP[2]);
  not not_3 (not_3_out, ALU_OP[1]);
  not not_4 (not_4_out, ALU_OP[0]);
  and and_1 (and_1_out, ADD_C, not_1_out, not_2_out, not_3_out, ALU_OP[0]);
  or or_1 (ALU_CARRY, and_1_out, and_2_out);
  and and_2 (and_2_out, SUB_C, not_1_out, not_2_out, ALU_OP[1], not_4_out);
endmodule

module bitwiseOps (
  input  [31:0] A,
  input  [31:0] B,
  output [31:0] AND_OUT,
  output [31:0] OR_OUT,
  output [31:0] NOT_OUT,
  output [31:0] XOR_OUT,
  output [31:0] NAND_OUT
);

  assign AND_OUT = A & B;  // AND_Gate and_1, 32 bits wide
  assign OR_OUT = A | B;  // OR_Gate or_1, 32 bits wide
  assign NOT_OUT = ~A;  // NOT_Gate not_1, 32 bits wide
  assign XOR_OUT = A ^ B;  // XOR_Gate xor_1, 32 bits wide
  assign NAND_OUT = ~(A & B);  // NAND_Gate nand_1, 32 bits wide
endmodule
