// Logisim project cpu - Copy.circ as structural Verilog: 9 circuits, main circuit CPU_Test
module main (
  input  RESET,
  input  CLK,
  input  [31:0] DATA_IN,
  output LOAD_RAM,
  output [15:0] ADR_OUT,
  output [31:0] DATA_OUT
);

  wire alu_1_qcarry, alu_1_qequal, alu_1_qgreater, alu_1_qless, alu_1_zerqo, CLK_t, CONSTANTV_0, CONSTANTV_1,
       d_ff_1_qn, FLAG_FALSE, HALT, HALTED, or_1_out;
  wire [2:0] FLAG_COND;
  wire [3:0] ALU_OP, counter_1_q, multiplexer_2_out, multiplexer_3_out, multiplexer_4_out, multiplexer_5_out;
  wire [7:0] INS_OPCODE;
  wire [23:0] INS_OUT;
  wire [28:0] MICROCODE;
  wire [31:0] ALU_OUT, alumux_1_q, alumux_1_q2, CONSTANT_OUT, registers_1_adr_out, registers_1_bp_out,
       registers_1_const_out, registers_1_ins_lit_out, registers_1_pc_out, registers_1_r1out,
       registers_1_r2out, registers_1_r3out, registers_1_r4out, registers_1_r5out, registers_1_r6out,
       registers_1_r7out, registers_1_r8out, registers_1_ram_out, registers_1_sp_out;

  D_Flip_Flop d_ff_1 (.D(1'b0), .clk(1'b0), .Q(HALTED), .Qn(d_ff_1_qn), .preset(HALT), .reset(RESET));
  LedBar ledbar_1 (
    .led0(INS_OPCODE[7]), .led1(INS_OPCODE[6]), .led2(INS_OPCODE[5]), .led3(INS_OPCODE[4]),
    .led4(INS_OPCODE[3]), .led5(INS_OPCODE[2]), .led6(INS_OPCODE[1]), .led7(INS_OPCODE[0]));
  LedBar #(.matrixcols(4)) ledbar_2 (.led0(INS_OUT[23]), .led1(INS_OUT[22]), .led2(INS_OUT[21]), .led3(INS_OUT[20]));
  LedBar #(.matrixcols(4)) ledbar_3 (.led0(INS_OUT[19]), .led1(INS_OUT[18]), .led2(INS_OUT[17]), .led3(INS_OUT[16]));
  and and_1 (CLK_t, CLK, d_ff_1_qn);
  LedBar #(.matrixcols(16)) ledbar_4 (
    .led0(INS_OUT[15]), .led1(INS_OUT[14]), .led2(INS_OUT[13]), .led3(INS_OUT[12]), .led4(INS_OUT[11]),
    .led5(INS_OUT[10]), .led6(INS_OUT[9]), .led7(INS_OUT[8]), .led8(INS_OUT[7]), .led9(INS_OUT[6]),
    .led10(INS_OUT[5]), .led11(INS_OUT[4]), .led12(INS_OUT[3]), .led13(INS_OUT[2]), .led14(INS_OUT[1]),
    .led15(INS_OUT[0]));
  LED ACTIVE (.in(d_ff_1_qn));
  Multiplexer #(.select(2), .width(32)) multiplexer_1 (
    .in0({32{1'b0}}), .in1(32'h1), .in2({32{1'b1}}), .out(CONSTANT_OUT), .sel({CONSTANTV_0, CONSTANTV_1}));  // open: in3
  Multiplexer #(.width(4)) multiplexer_2 (
    .in0(MICROCODE[3:0]), .in1(INS_OUT[23:20]), .out(multiplexer_2_out), .sel(MICROCODE[19]));
  Multiplexer #(.width(4)) multiplexer_3 (
    .in0(multiplexer_2_out), .in1(INS_OUT[19:16]), .out(multiplexer_3_out), .sel(MICROCODE[20]));
  Multiplexer #(.width(4)) multiplexer_4 (
    .in0(multiplexer_5_out), .in1(INS_OUT[19:16]), .out(multiplexer_4_out), .sel(MICROCODE[18]));
  Multiplexer #(.width(4)) multiplexer_5 (
    .in0(MICROCODE[7:4]), .in1(INS_OUT[23:20]), .out(multiplexer_5_out), .sel(MICROCODE[17]));
  registers registers_1 (
    .ADDRESS_16(ADR_OUT), .BP_OUT(registers_1_bp_out), .SP_OUT(registers_1_sp_out),
    .INS_OUT({INS_OPCODE, INS_OUT}), .PC_OUT(registers_1_pc_out), .RAM_OUT(registers_1_ram_out),
    .ADR_OUT(registers_1_adr_out), .CONST_OUT(registers_1_const_out), .INS_LIT_OUT(registers_1_ins_lit_out),
    .LOAD_RAM(LOAD_RAM), .R1OUT(registers_1_r1out), .R2OUT(registers_1_r2out), .R3OUT(registers_1_r3out),
    .R8OUT(registers_1_r8out), .R4OUT(registers_1_r4out), .R5OUT(registers_1_r5out),
    .R6OUT(registers_1_r6out), .R7OUT(registers_1_r7out), .DBUS(DATA_OUT), .CLK(CLK_t), .RESET(RESET),
    .ALU_VAL(ALU_OUT), .RAM_VAL(DATA_IN), .CONST_VAL(CONSTANT_OUT), .SP_DEC(MICROCODE[21]),
    .SP_COUNT(MICROCODE[16]), .PC_COUNT(MICROCODE[14]), .DLOAD(multiplexer_3_out), .DSTORE(multiplexer_4_out));
  ALUmux alumux_1 (
    .Q(alumux_1_q), .Q2(alumux_1_q2), .D1(registers_1_r1out), .D2(registers_1_r2out), .D3(registers_1_r3out),
    .D4(registers_1_r4out), .D5(registers_1_r5out), .D6(registers_1_r6out), .D7(registers_1_r7out),
    .D8(registers_1_r8out), .D9(registers_1_ram_out), .D10(registers_1_ins_lit_out),
    .D11(registers_1_adr_out), .D12(registers_1_pc_out), .D13(registers_1_const_out),
    .D14(registers_1_bp_out), .D15(registers_1_sp_out), .DREG2(INS_OUT[19:16]),
    .USE_CONST_AS_B(MICROCODE[28]), .USE_INS_LITERAL_AS_B(MICROCODE[27]), .DREG(INS_OUT[23:20]));
  ALU alu_1 (
    .QCARRY(alu_1_qcarry), .QGREATER(alu_1_qgreater), .QLESS(alu_1_qless), .ZERQO(alu_1_zerqo),
    .QEQUAL(alu_1_qequal), .ALU_OUT(ALU_OUT), .ALU_OP(ALU_OP), .INPUT_A(alumux_1_q), .INPUT_B(alumux_1_q2));
  flagregister flagregister_1 (
    .FLAG_FALSE(FLAG_FALSE), .F_Zero(alu_1_zerqo), .F_L(alu_1_qless), .F_Eq(alu_1_qequal),
    .F_G(alu_1_qgreater), .F_C(alu_1_qcarry), .UPDATE_FLAGS(MICROCODE[22]), .CLK(CLK_t), .RESET(RESET),
    .FLAG_CONDITION(FLAG_COND));
  or or_1 (or_1_out, FLAG_FALSE, MICROCODE[15]);
  Counter #(.max('hf), .width(4)) counter_1 (
    .load(or_1_out), .D(4'b0000), .count(1'b1), .Q(counter_1_q), .up(1'b1), .clk(CLK_t), .clr(RESET));  // open: carry
  ROM #(.addrWidth(12), .dataWidth(29)) ROM_1 (
    .addr({INS_OPCODE, counter_1_q}),
    .data({MICROCODE[28:27], FLAG_COND, HALT, MICROCODE[22:14], ALU_OP, CONSTANTV_0, CONSTANTV_1, MICROCODE[7:0]}));

  // Other names for the same wires on the sheet: INS_OUT[31:24] = INS_OPCODE; ADR16[15:0] = ADR_OUT;
  //   DBUS[31:0] = DATA_OUT; INS_REG_B[3:0] = INS_OUT[19:16]; INS_REG_A[3:0] = INS_OUT[23:20];
  //   REG_IN[3:0] = MICROCODE[3:0]; REG_OUT[3:0] = MICROCODE[7:4];
  //   MICROCODE (some bits) = {FLAG_COND, HALT, ALU_OP, CONSTANTV_0, CONSTANTV_1}; PC_COUNT = MICROCODE[14];
  //   MICROCODE_END = MICROCODE[15]; SP_COUNT = MICROCODE[16]; USE_INS_A_OUT = MICROCODE[17];
  //   USE_INS_B_OUT = MICROCODE[18]; USE_INS_A_IN = MICROCODE[19]; USE_INS_B_IN = MICROCODE[20];
  //   SP_DEC = MICROCODE[21]; UPDATE_FLAGS = MICROCODE[22]; USE_INS_LITERAL_AS_B = MICROCODE[27];
  //   USE_CONST_AS_B = MICROCODE[28]; RAM_IN = LOAD_RAM; RAM_OUT[31:0] = DATA_IN

  // Notes on the sheet:
  //   OPCODE
  //   CONTROL
  //   A
  //   B
  //   LITERAL
  //   0
  //   1
  //   -1
  //   unused
  //   contents of ROM_1 (hex, n*v repeats v):
  //   cb 409a 8000 13*0 cb 409a 8000 13*0 cb 409a 8000 13*0 cb 409a 8000 13*0 cb 409a 8000 13*0 cb 409a
  //   8000 13*0 cb 409a 8000 13*0 cb 409a 8000 13*0 cb 409a 8000 13*0 cb 409a 8000 13*0 cb 409a 8000 13*0
  //   cb 409a 8000 13*0 cb 409a 8000 13*0 cb 409a 8000 13*0 cb 409a 8000 13*0 cb 409a 8000 13*0 cb 409a
  //   10080500 8000 12*0 cb 409a 10080900 8000 12*0 cb 409a 8000 13*0 cb 409a 402800 8000 12*0 cb 409a
  //   80400 8000 12*0 cb 409a 80800 8000 12*0 cb 409a 80c00 8000 12*0 cb 409a 82c00 8000 12*0 cb 409a
  //   83000 8000 12*0 cb 409a 83400 8000 12*0 cb 409a 8000 13*0 cb 409a 8000 13*0 cb 409a 8000 13*0 cb
  //   409a 8000 13*0 cb 409a 8000 13*0 cb 409a 8000 13*0 cb 409a 83800 8000 12*0 cb 409a 83c00 8000 12*0
  //   cb 409a 8000 13*0 cb 409a 8000 13*0 cb 409a 8000 13*0 cb 409a 8000 13*0 cb 409a 8000 13*0 cb 409a
  //   8000 13*0 cb 409a 8000 13*0 cb 409a 8000 13*0 cb 409a 8000 13*0 cb 409a 8000 13*0 cb 409a 8000 13*0
  //   cb 409a 8000 13*0 cb 409a 8000 13*0 cb 409a 8000 13*0 cb 409a fb 2100c9 ac 8000 10*0 cb 409a 10000
  //   fb 9c 8000 10*0 cb 409a 8000 13*0 cb 409a fb 230009 8000 11*0 cb 409a 10000 fb 80090 8000 10*0 cb
  //   409a 8000 13*0 cb 409a 8000 13*0 cb 409a 8000 13*0 cb 409a 8000 13*0 cb 409a 8000 13*0 cb 409a 8000
  //   13*0 cb 409a 8000 13*0 cb 409a 8000 13*0 cb 409a 8000 13*0 cb 409a 8000 13*0 cb 409a 8000 13*0 cb
  //   409a 8000 13*0 cb 409a 8000 13*0 cb 409a 8000 13*0 cb 409a 8000 13*0 cb 409a 8000 13*0 cb 409a c0000
  //   8000 12*0 cb 409a 800a0 8000 12*0 cb 409a ab 80090 8000 11*0 cb 409a ab 9b 80090 8000 10*0 cb 409a
  //   ab 20009 8000 11*0 cb 409a 8000 13*0 cb 409a 8000 13*0 cb 409a 8000 13*0 cb 409a 8000 13*0 cb 409a
  //   8000 13*0 cb 409a 8000 13*0 cb 409a ab 9b 20009 8000 10*0 cb 409a 4000b 80090 8000 11*0 cb 409a
  //   2000b 40009 8000 11*0 cb 409a 800040b 40009 8000 11*0 cb 409a 800040b 100090 8000 11*0 cb 409a 8000
  //   13*0 cb 409a 8000 13*0 cb 409a 8000 13*0 cb 409a 8000 13*0 cb 409a 8000 13*0 cb 409a 8000 13*0 cb
  //   409a 8000 13*0 cb 409a 8000 13*0 cb 409a 8000 13*0 cb 409a 8000 13*0 cb 409a 8000 13*0 cb 409a 8000
  //   13*0 cb 409a 8000 13*0 cb 409a 8000 13*0 cb 409a 8000 13*0 cb 409a 8000 13*0 cb 409a 8000 13*0 cb
  //   409a 8000 13*0 cb 409a 8000 13*0 cb 409a 8000 13*0 cb 409a 8000 13*0 cb 409a 8000 13*0 cb 409a 8000
  //   13*0 cb 409a 8000 13*0 cb 409a 8000 13*0 cb 409a 8000 13*0 cb 409a 8000 13*0 cb 409a 8000 13*0 cb
  //   409a 8000 13*0 cb 409a 8000 13*0 cb 409a 8000 13*0 cb 409a 8000 13*0 cb 409a 8000 13*0 cb 409a 8000
  //   13*0 cb 409a 8000 13*0 cb 409a 8000 13*0 cb 409a 8000 13*0 cb 409a 8000 13*0 cb 409a 8000 13*0 cb
  //   409a 8000 13*0 cb 409a 8000 13*0 cb 409a 8000 13*0 cb 409a 8000 13*0 cb 409a 8000 13*0 cb 409a 8000
  //   13*0 cb 409a 8000 13*0 cb 409a 8000 13*0 cb 409a 8000 13*0 cb 409a 8000 13*0 cb 409a 8000 13*0 cb
  //   409a 8000 13*0 cb 409a 8000 13*0 cb 409a 8000 13*0 cb 409a 8000 13*0 cb 409a 8000 13*0 cb 409a 8000
  //   13*0 cb 409a 8000 13*0 cb 409a 8000 13*0 cb 409a 8000 13*0 cb 409a 8000 13*0 cb 409a 8000 13*0 cb
  //   409a 8000 13*0 cb 409a 8000 13*0 cb 409a 8000 13*0 cb 409a 8000 13*0 cb 409a 8000 13*0 cb 409a 8000
  //   13*0 cb 409a 8000 13*0 cb 409a 800000 13*0 cb 409a 8000 13*0 cb 409a 8000 13*0 cb 409a 8000 13*0 cb
  //   409a 8000 13*0 cb 409a 8000 13*0 cb 409a 8000 13*0 cb 409a 8083800 8000 12*0 cb 409a 8083c00 8000
  //   12*0 cb 409a 8000 13*0 cb 409a 8402800 8000 12*0 cb 409a 8080400 8000 12*0 cb 409a 8080800 8000 12*0
  //   cb 409a 8080c00 8000 12*0 cb 409a 8082c00 8000 12*0 cb 409a 8083000 8000 12*0 cb 409a 8000 13*0 cb
  //   409a 8000 13*0 cb 409a 8000 13*0 cb 409a 8000 13*0 cb 409a 8000 13*0 cb 409a 8000 13*0 cb 409a 8000
  //   13*0 cb 409a 8000 13*0 cb 409a 8000 13*0 cb 409a 8000 13*0 cb 409a 8000 13*0 cb 409a 8000 13*0 cb
  //   409a 8000 13*0 cb 409a 8000 13*0 cb 409a 8000 13*0 cb 409a 8000 13*0 cb 409a 8000 13*0 cb 409a 8000
  //   13*0 cb 409a 8000 13*0 cb 409a 8000 13*0 cb 409a 8000 13*0 cb 409a 8000 13*0 cb 409a 8000 13*0 cb
  //   409a 8000 13*0 cb 409a 8000 13*0 cb 409a 8000 13*0 cb 409a 8000 13*0 cb 409a 8000 13*0 cb 409a 8000
  //   13*0 cb 409a 8000 13*0 cb 409a 8000 13*0 cb 409a 8000 13*0 cb 409a 8000 13*0 cb 409a 8000 13*0 cb
  //   409a 8000 13*0 cb 409a 8000 13*0 cb 409a 8000 1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
endmodule

module alucarry (
  input  ADD_C,
  input  SUB_C,
  input  [3:0] ALU_OP,
  output ALU_CARRY
);

  wire and_1_out, and_2_out, not_1_out, not_2_out, not_3_out, not_4_out;

  not not_1 (not_1_out, ALU_OP[3]);
  not not_2 (not_2_out, ALU_OP[2]);
  not not_3 (not_3_out, ALU_OP[1]);
  not not_4 (not_4_out, ALU_OP[0]);
  and and_1 (and_1_out, ADD_C, not_1_out, not_2_out, not_3_out, ALU_OP[0]);
  or or_1 (ALU_CARRY, and_1_out, and_2_out);
  and and_2 (and_2_out, SUB_C, not_1_out, not_2_out, ALU_OP[1], not_4_out);
endmodule

module bitwiseOps (
  input  [31:0] A,
  input  [31:0] B,
  output [31:0] AND_OUT,
  output [31:0] OR_OUT,
  output [31:0] NOT_OUT,
  output [31:0] XOR_OUT,
  output [31:0] NAND_OUT
);

  assign AND_OUT = A & B;  // AND_Gate and_1, 32 bits wide
  assign OR_OUT = A | B;  // OR_Gate or_1, 32 bits wide
  assign NOT_OUT = ~A;  // NOT_Gate not_1, 32 bits wide
  assign XOR_OUT = A ^ B;  // XOR_Gate xor_1, 32 bits wide
  assign NAND_OUT = ~(A & B);  // NAND_Gate nand_1, 32 bits wide
endmodule

module memorymap (
  input  WRITE,
  input  [15:0] ADR,
  output OUT_VAL,
  output ROM_VAL
);

  wire nand_1_out, not_1_out, not_2_out, not_3_out, not_4_out, not_5_out, not_6_out, not_7_out, not_8_out,
       not_9_out, not_10_out, not_11_out, not_12_out, not_13_out, not_14_out, not_15_out;

  not not_1 (not_1_out, ADR[0]);
  not not_2 (not_2_out, ADR[1]);
  not not_3 (not_3_out, ADR[2]);
  not not_4 (not_4_out, ADR[3]);
  not not_5 (not_5_out, ADR[4]);
  not not_6 (not_6_out, ADR[5]);
  not not_7 (not_7_out, ADR[6]);
  not not_8 (not_8_out, ADR[7]);
  not not_9 (not_9_out, ADR[8]);
  not not_10 (not_10_out, ADR[9]);
  not not_11 (not_11_out, ADR[10]);
  not not_12 (not_12_out, ADR[11]);
  not not_13 (not_13_out, ADR[12]);
  not not_14 (not_14_out, ADR[15]);
  nand nand_1 (nand_1_out, not_1_out, not_2_out, not_3_out, not_4_out, not_5_out, not_6_out, not_7_out, not_8_out, not_9_out, not_10_out, not_11_out, not_12_out, not_13_out, ADR[13], ADR[14], not_14_out, 1'b1);
  not not_15 (not_15_out, nand_1_out);
  LED TO_OUT (.in(OUT_VAL));
  and and_1 (OUT_VAL, WRITE, not_15_out);
  and and_2 (ROM_VAL, nand_1_out, WRITE);
  LED TO_RAM (.in(ROM_VAL));
endmodule

module ALU (
  input  [3:0] ALU_OP,
  input  [31:0] INPUT_A,
  input  [31:0] INPUT_B,
  output QCARRY,
  output [31:0] ALU_OUT,
  output QGREATER,
  output QLESS,
  output ZERQO,
  output QEQUAL
);

  wire ADD_C, and_1_out, comparator_1_eq, comparator_1_gt, comparator_1_lt, comparator_2_eq, SUB_C;
  wire [4:0] bitselector_1_out, bitselector_2_out, bitselector_3_out, bitselector_4_out, bitselector_5_out;
  wire [31:0] adder_1_out, bitwiseops_1_and_out, bitwiseops_1_nand_out, bitwiseops_1_not_out,
       bitwiseops_1_or_out, bitwiseops_1_xor_out, multiplier_1_out, negator_1_out, shifter_1_out,
       shifter_2_out, shifter_3_out, shifter_4_out, shifter_5_out, subtractor_1_out;

  BitSelector #(.group(5), .width(32)) bitselector_1 (.in(INPUT_B), .out(bitselector_1_out), .sel(3'b000));
  BitSelector #(.group(5), .width(32)) bitselector_2 (.in(INPUT_B), .out(bitselector_2_out), .sel(3'b000));
  BitSelector #(.group(5), .width(32)) bitselector_3 (.in(INPUT_B), .out(bitselector_3_out), .sel(3'b000));
  BitSelector #(.group(5), .width(32)) bitselector_4 (.in(INPUT_B), .out(bitselector_4_out), .sel(3'b000));
  BitSelector #(.group(5), .width(32)) bitselector_5 (.in(INPUT_B), .out(bitselector_5_out), .sel(3'b000));
  Adder #(.width(32)) adder_1 (.a(INPUT_A), .b(INPUT_B), .out(adder_1_out), .cin(1'b0), .cout(ADD_C));
  Subtractor #(.width(32)) subtractor_1 (.a(INPUT_A), .b(INPUT_B), .out(subtractor_1_out), .bin(1'b0), .bout(SUB_C));
  Multiplier #(.width(32)) multiplier_1 (.a(INPUT_A), .b(INPUT_B), .out(multiplier_1_out));  // open: cin, cout
  Negator #(.width(32)) negator_1 (.in(INPUT_A), .out(negator_1_out));
  Shifter #(.width(32)) shifter_1 (.in(INPUT_A), .\dist (bitselector_1_out), .out(shifter_1_out));
  Shifter #(.shift("lr"), .width(32)) shifter_2 (.in(INPUT_A), .\dist (bitselector_2_out), .out(shifter_2_out));
  Shifter #(.shift("ar"), .width(32)) shifter_3 (.in(INPUT_A), .\dist (bitselector_3_out), .out(shifter_3_out));
  Shifter #(.shift("rl"), .width(32)) shifter_4 (.in(INPUT_A), .\dist (bitselector_4_out), .out(shifter_4_out));
  Shifter #(.shift("rr"), .width(32)) shifter_5 (.in(INPUT_A), .\dist (bitselector_5_out), .out(shifter_5_out));
  Comparator #(.width(32)) comparator_1 (
    .a(INPUT_A), .b(INPUT_B), .gt(comparator_1_gt), .eq(comparator_1_eq), .lt(comparator_1_lt));
  bitwiseOps bitwiseops_1 (
    .AND_OUT(bitwiseops_1_and_out), .OR_OUT(bitwiseops_1_or_out), .NOT_OUT(bitwiseops_1_not_out),
    .XOR_OUT(bitwiseops_1_xor_out), .NAND_OUT(bitwiseops_1_nand_out), .A(INPUT_A), .B(INPUT_B));
  alucarry alucarry_1 (.ALU_CARRY(QCARRY), .SUB_C(SUB_C), .ALU_OP(ALU_OP), .ADD_C(ADD_C));
  Multiplexer #(.select(4), .width(32)) multiplexer_1 (
    .in0({32{1'b0}}), .in1(adder_1_out), .in2(subtractor_1_out), .in3(multiplier_1_out), .in4(negator_1_out),
    .in5(shifter_1_out), .in6(shifter_2_out), .in7(shifter_3_out), .in8(shifter_4_out), .in9(shifter_5_out),
    .in10({32{1'b0}}), .in11(bitwiseops_1_and_out), .in12(bitwiseops_1_or_out), .in13(bitwiseops_1_not_out),
    .in14(bitwiseops_1_xor_out), .in15(bitwiseops_1_nand_out), .out(ALU_OUT), .sel(ALU_OP));
  and and_1 (and_1_out, 1'b1, ALU_OP[3], ~ALU_OP[2], ALU_OP[1], ~ALU_OP[0]);  // AND_Gate
  and and_2 (QGREATER, and_1_out, comparator_1_gt);
  and and_3 (QLESS, and_1_out, comparator_1_lt);
  and and_4 (ZERQO, comparator_2_eq, ~and_1_out);  // AND_Gate
  and and_5 (QEQUAL, and_1_out, comparator_1_eq);
  Comparator #(.width(32)) comparator_2 (.a(ALU_OUT), .b({32{1'b0}}), .eq(comparator_2_eq));  // open: gt, lt
endmodule

module flagregister (
  input  F_Zero,
  input  F_L,
  input  F_Eq,
  input  F_G,
  input  [2:0] FLAG_CONDITION,
  input  F_C,
  input  UPDATE_FLAGS,
  input  CLK,
  input  RESET,
  output FLAG_FALSE
);

  wire not_1_out, not_2_out, not_3_out, not_4_out, not_5_out;
  wire [4:0] register_1_q;

  Register #(.width(5)) register_1 (
    .D({F_C, F_G, F_Eq, F_L, F_Zero}), .en(UPDATE_FLAGS), .clk(CLK), .Q(register_1_q), .clr(RESET));
  LED Z (.in(register_1_q[0]));
  LED L (.in(register_1_q[1]));
  LED EQ (.in(register_1_q[2]));
  LED G (.in(register_1_q[3]));
  LED C (.in(register_1_q[4]));
  not not_1 (not_1_out, register_1_q[0]);
  not not_2 (not_2_out, register_1_q[1]);
  not not_3 (not_3_out, register_1_q[3]);
  not not_4 (not_4_out, register_1_q[2]);
  not not_5 (not_5_out, register_1_q[4]);
  Multiplexer #(.select(3)) multiplexer_1 (
    .in0(1'b0), .in1(register_1_q[0]), .in2(not_1_out), .in3(not_2_out), .in4(not_3_out), .in5(not_4_out),
    .in6(register_1_q[2]), .in7(not_5_out), .out(FLAG_FALSE), .sel(FLAG_CONDITION));

  // Notes on the sheet:
  //   Z L E G C
  //   NONE
  //   JNZ
  //   JZ
  //   JL
  //   JG
  //   JE
  //   JNE
  //   JC
endmodule

module ALUmux (
  input  USE_CONST_AS_B,
  input  USE_INS_LITERAL_AS_B,
  input  [31:0] D1,
  input  [31:0] D2,
  input  [31:0] D3,
  input  [31:0] D4,
  input  [31:0] D5,
  input  [31:0] D6,
  input  [31:0] D7,
  input  [31:0] D8,
  input  [31:0] D9,
  input  [31:0] D10,
  input  [31:0] D11,
  input  [31:0] D12,
  input  [31:0] D13,
  input  [31:0] D14,
  input  [31:0] D15,
  input  [3:0] DREG2,
  input  [3:0] DREG,
  output [31:0] Q2,
  output [31:0] Q
);

  wire [31:0] multiplexer_1_out, multiplexer_2_out;

  Multiplexer #(.width(32)) multiplexer_1 (.in0(multiplexer_2_out), .in1(D10), .out(multiplexer_1_out));  // open: sel
  Multiplexer #(.select(4), .width(32)) multiplexer_2 (
    .in0({32{1'b0}}), .in1(D1), .in2(D2), .in3(D3), .in4(D4), .in5(D5), .in6(D6), .in7(D7), .in8(D8),
    .in9(D9), .in10(D10), .in11(D11), .in12(D12), .in13(D13), .in14(D14), .in15(D15),
    .out(multiplexer_2_out), .sel(DREG2));
  Multiplexer #(.select(4), .width(32)) multiplexer_3 (
    .in0({32{1'b0}}), .in1(D1), .in2(D2), .in3(D3), .in4(D4), .in5(D5), .in6(D6), .in7(D7), .in8(D8),
    .in9(D9), .in10(D10), .in11(D11), .in12(D12), .in13(D13), .in14(D14), .in15(D15), .out(Q), .sel(DREG));
  Multiplexer #(.width(32)) multiplexer_4 (.in0(multiplexer_1_out), .in1(D13), .out(Q2));  // open: sel
endmodule

module registers (
  input  CLK,
  input  RESET,
  input  SP_DEC,
  input  SP_COUNT,
  input  PC_COUNT,
  input  [3:0] DLOAD,
  input  [31:0] ALU_VAL,
  input  [31:0] RAM_VAL,
  input  [31:0] CONST_VAL,
  input  [3:0] DSTORE,
  output [31:0] R1OUT,
  output [31:0] R2OUT,
  output [31:0] SP_OUT,
  output [31:0] R3OUT,
  output [31:0] BP_OUT,
  output LOAD_RAM,
  output [31:0] INS_OUT,
  output [31:0] R4OUT,
  output [31:0] R5OUT,
  output [31:0] INS_LIT_OUT,
  output [31:0] PC_OUT,
  output [31:0] R6OUT,
  output [31:0] ADR_OUT,
  output [31:0] R7OUT,
  output [15:0] ADDRESS_16,
  output [31:0] R8OUT,
  output [31:0] DBUS,
  output [31:0] RAM_OUT,
  output [31:0] CONST_OUT
);

  wire ADR_IN, BP_IN, INS_IN, JMP_IN, not_1_out, R1IN, R2IN, R3IN, R4IN, R5IN, R6IN, R7IN, R8IN, SP_IN;
  wire [15:0] bitselector_1_out, bitselector_2_out;

  Register #(.width(32)) R1 (.D(DBUS), .en(R1IN), .clk(CLK), .Q(R1OUT), .clr(RESET));
  Register #(.width(32)) R2 (.D(DBUS), .en(R2IN), .clk(CLK), .Q(R2OUT), .clr(RESET));
  Register #(.width(32)) R3 (.D(DBUS), .en(R3IN), .clk(CLK), .Q(R3OUT), .clr(RESET));
  Register #(.width(32)) R4 (.D(DBUS), .en(R4IN), .clk(CLK), .Q(R4OUT), .clr(RESET));
  Register #(.width(32)) R5 (.D(DBUS), .en(R5IN), .clk(CLK), .Q(R5OUT), .clr(RESET));
  Register #(.width(32)) R6 (.D(DBUS), .en(R6IN), .clk(CLK), .Q(R6OUT), .clr(RESET));
  Register #(.width(32)) R7 (.D(DBUS), .en(R7IN), .clk(CLK), .Q(R7OUT), .clr(RESET));
  Register #(.width(32)) R8 (.D(DBUS), .en(R8IN), .clk(CLK), .Q(R8OUT), .clr(RESET));
  Multiplexer #(.select(4), .width(32)) multiplexer_1 (
    .in0(ALU_VAL), .in1(R1OUT), .in2(R2OUT), .in3(R3OUT), .in4(R4OUT), .in5(R5OUT), .in6(R6OUT), .in7(R7OUT),
    .in8(R8OUT), .in9(RAM_VAL), .in10(INS_LIT_OUT), .in11(ADR_OUT), .in12(PC_OUT), .in13(CONST_VAL),
    .in14(BP_OUT), .in15(SP_OUT), .out(DBUS), .sel(DSTORE));
  not not_1 (not_1_out, SP_DEC);
  Register #(.width(32)) RBP (.D(DBUS), .en(BP_IN), .clk(CLK), .Q(BP_OUT), .clr(RESET));
  Register #(.width(32)) RINS (.D(DBUS), .en(INS_IN), .clk(CLK), .Q(INS_OUT), .clr(RESET));
  Register #(.width(16)) RADR (.D(bitselector_1_out), .en(ADR_IN), .clk(CLK), .Q(ADDRESS_16), .clr(RESET));
  BitSelector #(.group(16), .width(32)) bitselector_1 (.in(DBUS), .out(bitselector_1_out), .sel(1'b0));
  Counter #(.max('hffffffff), .width(32)) RSP (
    .load(SP_IN), .D(DBUS), .count(SP_COUNT), .Q(SP_OUT), .up(not_1_out), .clk(CLK), .clr(RESET));  // open: carry
  Counter #(.max('hffffffff), .width(32)) counter_1 (
    .load(JMP_IN), .D(DBUS), .count(PC_COUNT), .Q(PC_OUT), .up(1'b1), .clk(CLK), .clr(RESET));  // open: carry
  assign ADR_OUT = {{16{1'b0}}, ADDRESS_16};  // Bit_Extender bit_extender_1
  BitSelector #(.group(16), .width(32)) bitselector_2 (.in(INS_OUT), .out(bitselector_2_out), .sel(1'b0));
  assign INS_LIT_OUT = {{16{1'b0}}, bitselector_2_out};  // Bit_Extender bit_extender_2
  Demultiplexer #(.select(4)) demultiplexer_1 (
    .out1(R1IN), .out2(R2IN), .out3(R3IN), .out4(R4IN), .out5(R5IN), .out6(R6IN), .out7(R7IN), .out8(R8IN),
    .out9(LOAD_RAM), .out10(INS_IN), .out11(ADR_IN), .out12(JMP_IN), .out14(BP_IN), .out15(SP_IN), .in(1'b1),
    .sel(DLOAD));  // open: out0, out13

  assign CONST_OUT = CONST_VAL;
  assign RAM_OUT = RAM_VAL;

  // Other names for the same wires on the sheet: ALU_OUT[31:0] = ALU_VAL; CONSTANT_OUT[31:0] = CONST_VAL;
  //   INS_LITERAL[31:0] = INS_LIT_OUT
endmodule

module CPU_Test (
);

  wire CLK_out, clock_1_out, main_1_load_ram, memorymap_1_out_val, memorymap_1_rom_val, or_1_out, RESET_out;
  wire [6:0] bitselector_1_out;
  wire [15:0] main_1_adr_out;
  wire [31:0] main_1_data_out, RAM_1_dout;

  or or_1 (or_1_out, CLK_out, clock_1_out);
  Clock clock_1 (.out(clock_1_out));
  Button RESET (.out(RESET_out));
  Button CLK (.out(CLK_out));
  main main_1 (
    .LOAD_RAM(main_1_load_ram), .ADR_OUT(main_1_adr_out), .DATA_OUT(main_1_data_out), .RESET(RESET_out),
    .CLK(or_1_out), .DATA_IN(RAM_1_dout));
  memorymap memorymap_1 (
    .OUT_VAL(memorymap_1_out_val), .ROM_VAL(memorymap_1_rom_val), .WRITE(main_1_load_ram),
    .ADR(main_1_adr_out));
  RAM #(.addrWidth(16), .asyncread("true"), .dataWidth(32), .\type ("nonvolatile")) RAM_1 (
    .addr(main_1_adr_out), .we(memorymap_1_rom_val), .oe(1'b1), .clk(or_1_out), .din(main_1_data_out),
    .dout(RAM_1_dout));
  TTY tty_1 (.data(bitselector_1_out), .clk(or_1_out), .we(memorymap_1_out_val), .clr(RESET_out));
  BitSelector #(.group(7), .width(32)) bitselector_1 (.in(main_1_data_out), .out(bitselector_1_out), .sel(3'b000));
endmodule
