// Logisim project ttltest.circ as structural Verilog: 1 circuit, main circuit main
module main (
  input  [31:0] in_1,
  input  in_2,
  input  in_3
);

  wire CLK_out, CLR_out, n74125_1_pin3, n74125_1_pin6, n74125_1_pin8, n74125_1_pin11, n74125_2_pin3,
       n74125_2_pin6, n74125_2_pin8, n74125_2_pin11, n74125_3_pin3, n74125_3_pin6, n74125_3_pin8,
       n74125_3_pin11, n74125_4_pin3, n74125_4_pin6, n74125_4_pin8, n74125_4_pin11, n74125_5_pin3,
       n74125_5_pin6, n74125_5_pin8, n74125_5_pin11, n74125_6_pin3, n74125_6_pin6, n74125_6_pin8,
       n74125_6_pin11, n74125_7_pin3, n74125_7_pin6, n74125_7_pin8, n74125_7_pin11, n74125_8_pin3,
       n74125_8_pin6, n74125_8_pin8, n74125_8_pin11, n74175_1_pin2, n74175_1_pin7, n74175_1_pin10,
       n74175_1_pin15, n74175_2_pin2, n74175_2_pin7, n74175_2_pin10, n74175_2_pin15, n74175_3_pin2,
       n74175_3_pin7, n74175_3_pin10, n74175_3_pin15, n74175_4_pin2, n74175_4_pin7, n74175_4_pin10,
       n74175_4_pin15, n74175_5_pin2, n74175_5_pin7, n74175_5_pin10, n74175_5_pin15, n74175_6_pin2,
       n74175_6_pin7, n74175_6_pin10, n74175_6_pin15, n74175_7_pin2, n74175_7_pin7, n74175_7_pin10,
       n74175_7_pin15, n74175_8_pin2, n74175_8_pin7, n74175_8_pin10, n74175_8_pin15;

  Button CLK (.out(CLK_out));
  Button CLR (.out(CLR_out));
  _74175 #(.ShowInternalStructure("true")) u_74175_1 (
    .pin1(CLR_out), .pin2(n74175_1_pin2), .pin4(in_1[31]), .pin5(in_1[28]), .pin7(n74175_1_pin7),
    .pin15(n74175_1_pin15), .pin13(in_1[30]), .pin12(in_1[29]), .pin10(n74175_1_pin10), .pin9(CLK_out));  // open: pin3, pin6, pin14, pin11
  _74125 #(.ShowInternalStructure("true")) u_74125_1 (
    .pin1(in_2), .pin2(n74175_1_pin15), .pin3(n74125_1_pin3), .pin4(in_2), .pin5(n74175_1_pin10),
    .pin6(n74125_1_pin6), .pin13(in_2), .pin12(n74175_1_pin2), .pin11(n74125_1_pin11), .pin10(in_2),
    .pin9(n74175_1_pin7), .pin8(n74125_1_pin8));
  _74175 #(.ShowInternalStructure("true")) u_74175_2 (
    .pin1(CLR_out), .pin2(n74175_2_pin2), .pin4(in_1[27]), .pin5(in_1[24]), .pin7(n74175_2_pin7),
    .pin15(n74175_2_pin15), .pin13(in_1[26]), .pin12(in_1[25]), .pin10(n74175_2_pin10), .pin9(CLK_out));  // open: pin3, pin6, pin14, pin11
  _74125 #(.ShowInternalStructure("true")) u_74125_2 (
    .pin1(in_2), .pin2(n74175_2_pin15), .pin3(n74125_2_pin3), .pin4(in_2), .pin5(n74175_2_pin10),
    .pin6(n74125_2_pin6), .pin13(in_2), .pin12(n74175_2_pin2), .pin11(n74125_2_pin11), .pin10(in_2),
    .pin9(n74175_2_pin7), .pin8(n74125_2_pin8));
  _74175 #(.ShowInternalStructure("true")) u_74175_3 (
    .pin1(CLR_out), .pin2(n74175_3_pin2), .pin4(in_1[23]), .pin5(in_1[20]), .pin7(n74175_3_pin7),
    .pin15(n74175_3_pin15), .pin13(in_1[22]), .pin12(in_1[21]), .pin10(n74175_3_pin10), .pin9(CLK_out));  // open: pin3, pin6, pin14, pin11
  _74125 #(.ShowInternalStructure("true")) u_74125_3 (
    .pin1(in_2), .pin2(n74175_3_pin15), .pin3(n74125_3_pin3), .pin4(in_2), .pin5(n74175_3_pin10),
    .pin6(n74125_3_pin6), .pin13(in_2), .pin12(n74175_3_pin2), .pin11(n74125_3_pin11), .pin10(in_2),
    .pin9(n74175_3_pin7), .pin8(n74125_3_pin8));
  _74175 #(.ShowInternalStructure("true")) u_74175_4 (
    .pin1(CLR_out), .pin2(n74175_4_pin2), .pin4(in_1[19]), .pin5(in_1[16]), .pin7(n74175_4_pin7),
    .pin15(n74175_4_pin15), .pin13(in_1[18]), .pin12(in_1[17]), .pin10(n74175_4_pin10), .pin9(CLK_out));  // open: pin3, pin6, pin14, pin11
  _74125 #(.ShowInternalStructure("true")) u_74125_4 (
    .pin1(in_2), .pin2(n74175_4_pin15), .pin3(n74125_4_pin3), .pin4(in_2), .pin5(n74175_4_pin10),
    .pin6(n74125_4_pin6), .pin13(in_2), .pin12(n74175_4_pin2), .pin11(n74125_4_pin11), .pin10(in_2),
    .pin9(n74175_4_pin7), .pin8(n74125_4_pin8));
  _74175 #(.ShowInternalStructure("true")) u_74175_5 (
    .pin1(CLR_out), .pin2(n74175_5_pin2), .pin4(in_1[15]), .pin5(in_1[12]), .pin7(n74175_5_pin7),
    .pin15(n74175_5_pin15), .pin13(in_1[14]), .pin12(in_1[13]), .pin10(n74175_5_pin10), .pin9(CLK_out));  // open: pin3, pin6, pin14, pin11
  _74125 #(.ShowInternalStructure("true")) u_74125_5 (
    .pin1(in_2), .pin2(n74175_5_pin15), .pin3(n74125_5_pin3), .pin4(in_2), .pin5(n74175_5_pin10),
    .pin6(n74125_5_pin6), .pin13(in_2), .pin12(n74175_5_pin2), .pin11(n74125_5_pin11), .pin10(in_2),
    .pin9(n74175_5_pin7), .pin8(n74125_5_pin8));
  _74175 #(.ShowInternalStructure("true")) u_74175_6 (
    .pin1(CLR_out), .pin2(n74175_6_pin2), .pin4(in_1[11]), .pin5(in_1[8]), .pin7(n74175_6_pin7),
    .pin15(n74175_6_pin15), .pin13(in_1[10]), .pin12(in_1[9]), .pin10(n74175_6_pin10), .pin9(CLK_out));  // open: pin3, pin6, pin14, pin11
  _74125 #(.ShowInternalStructure("true")) u_74125_6 (
    .pin1(in_2), .pin2(n74175_6_pin15), .pin3(n74125_6_pin3), .pin4(in_2), .pin5(n74175_6_pin10),
    .pin6(n74125_6_pin6), .pin13(in_2), .pin12(n74175_6_pin2), .pin11(n74125_6_pin11), .pin10(in_2),
    .pin9(n74175_6_pin7), .pin8(n74125_6_pin8));
  _74175 #(.ShowInternalStructure("true")) u_74175_7 (
    .pin1(CLR_out), .pin2(n74175_7_pin2), .pin4(in_1[7]), .pin5(in_1[4]), .pin7(n74175_7_pin7),
    .pin15(n74175_7_pin15), .pin13(in_1[6]), .pin12(in_1[5]), .pin10(n74175_7_pin10), .pin9(CLK_out));  // open: pin3, pin6, pin14, pin11
  _74125 #(.ShowInternalStructure("true")) u_74125_7 (
    .pin1(in_2), .pin2(n74175_7_pin15), .pin3(n74125_7_pin3), .pin4(in_2), .pin5(n74175_7_pin10),
    .pin6(n74125_7_pin6), .pin13(in_2), .pin12(n74175_7_pin2), .pin11(n74125_7_pin11), .pin10(in_2),
    .pin9(n74175_7_pin7), .pin8(n74125_7_pin8));
  _74175 #(.ShowInternalStructure("true")) u_74175_8 (
    .pin1(CLR_out), .pin2(n74175_8_pin2), .pin4(in_1[3]), .pin5(in_1[0]), .pin7(n74175_8_pin7),
    .pin15(n74175_8_pin15), .pin13(in_1[2]), .pin12(in_1[1]), .pin10(n74175_8_pin10), .pin9(CLK_out));  // open: pin3, pin6, pin14, pin11
  _74125 #(.ShowInternalStructure("true")) u_74125_8 (
    .pin1(in_2), .pin2(n74175_8_pin15), .pin3(n74125_8_pin3), .pin4(in_2), .pin5(n74175_8_pin10),
    .pin6(n74125_8_pin6), .pin13(in_2), .pin12(n74175_8_pin2), .pin11(n74125_8_pin11), .pin10(in_2),
    .pin9(n74175_8_pin7), .pin8(n74125_8_pin8));
endmodule
